// Logisim project contador JS.circ as structural Verilog: 1 circuit, main circuit main
module main (
  input  D0,
  input  Tz,
  input  in_3,
  input  D0_2,
  input  D1,
  input  D1_2,
  input  D2,
  input  D2_2,
  input  D3,
  input  D3_2,
  output out_11,
  output out_12,
  output out_13,
  output out_14,
  output out_15,
  output out_16,
  output out_17,
  output out_18,
  output out_19
);

  wire and_2_out, and_3_out, and_4_out, and_5_out, and_6_out, and_7_out, and_8_out, and_9_out, and_10_out,
       and_11_out, and_12_out, and_13_out, and_14_out, and_15_out, and_16_out, and_17_out, and_18_out,
       and_19_out, and_20_out, and_21_out, and_22_out, and_23_out, and_24_out, and_25_out, and_26_out,
       clock_1_out, not_1_out, not_2_out, not_3_out, not_4_out, or_1_out, or_2_out, or_3_out, or_4_out,
       or_5_out, or_6_out, or_7_out, or_8_out, or_9_out, or_10_out, or_11_out, or_12_out, or_13_out,
       or_14_out, or_15_out, or_16_out, xor_1_out, xor_2_out, xor_3_out, xor_4_out, xor_5_out, xor_6_out,
       xor_7_out, xor_8_out;

  or or_1 (or_1_out, not_2_out, in_3);
  not not_1 (not_1_out, or_1_out);
  and and_1 (out_13, Tz, or_8_out);
  and and_2 (and_2_out, not_1_out, out_13);
  xor xor_1 (xor_1_out, and_2_out, out_11);
  and and_3 (and_3_out, and_2_out, xor_1_out);
  and and_4 (and_4_out, and_3_out, xor_2_out);
  and and_5 (and_5_out, and_4_out, xor_3_out);
  xor xor_2 (xor_2_out, and_3_out, out_14);
  xor xor_3 (xor_3_out, and_4_out, out_16);
  xor xor_4 (xor_4_out, and_5_out, out_18);
  and and_6 (and_6_out, or_1_out, D0);
  and and_7 (and_7_out, xor_1_out, not_1_out);
  and and_8 (and_8_out, or_1_out, D1);
  and and_9 (and_9_out, xor_2_out, not_1_out);
  and and_10 (and_10_out, or_1_out, D2);
  and and_11 (and_11_out, xor_3_out, not_1_out);
  and and_12 (and_12_out, or_1_out, D3_2);
  and and_13 (and_13_out, xor_4_out, not_1_out);
  or or_2 (or_2_out, and_6_out, and_7_out);
  or or_3 (or_3_out, and_8_out, and_9_out);
  or or_4 (or_4_out, and_10_out, and_11_out);
  or or_5 (or_5_out, and_12_out, and_13_out);
  D_Flip_Flop d_ff_1 (.clk(or_6_out), .D(or_2_out), .Q(out_11));  // open: Qn, preset, en, reset
  D_Flip_Flop d_ff_2 (.clk(or_6_out), .D(or_3_out), .Q(out_14));  // open: Qn, preset, en, reset
  D_Flip_Flop d_ff_3 (.clk(or_6_out), .D(or_4_out), .Q(out_16));  // open: Qn, preset, en, reset
  D_Flip_Flop d_ff_4 (.clk(or_6_out), .D(or_5_out), .Q(out_18));  // open: Qn, preset, en, reset
  or or_6 (or_6_out, clock_1_out, or_16_out);
  or or_7 (or_7_out, out_11, out_16, out_18, out_14);
  not not_2 (not_2_out, or_7_out);
  or or_8 (or_8_out, or_7_out, or_16_out);
  or or_9 (or_9_out, not_4_out, in_3);
  not not_3 (not_3_out, or_9_out);
  and and_14 (and_14_out, Tz, or_8_out);
  or or_10 (or_10_out, and_14_out, D0_2);
  or or_11 (or_11_out, D3, and_14_out);
  and and_15 (and_15_out, not_3_out, and_14_out);
  and and_16 (and_16_out, and_15_out, xor_5_out);
  and and_17 (and_17_out, and_16_out, xor_6_out);
  xor xor_5 (xor_5_out, and_15_out, out_12);
  xor xor_6 (xor_6_out, and_16_out, out_15);
  xor xor_7 (xor_7_out, and_17_out, out_17);
  and and_18 (and_18_out, and_17_out, xor_7_out);
  xor xor_8 (xor_8_out, and_18_out, out_19);
  and and_19 (and_19_out, or_9_out, or_10_out);
  and and_20 (and_20_out, xor_5_out, not_3_out);
  and and_21 (and_21_out, or_9_out, D1_2);
  and and_22 (and_22_out, xor_6_out, not_3_out);
  and and_23 (and_23_out, or_9_out, D2_2);
  and and_24 (and_24_out, xor_7_out, not_3_out);
  and and_25 (and_25_out, or_9_out, or_11_out);
  and and_26 (and_26_out, xor_8_out, not_3_out);
  or or_12 (or_12_out, and_19_out, and_20_out);
  or or_13 (or_13_out, and_21_out, and_22_out);
  or or_14 (or_14_out, and_23_out, and_24_out);
  Clock clock_1 (.out(clock_1_out));
  or or_15 (or_15_out, and_25_out, and_26_out);
  D_Flip_Flop d_ff_5 (.clk(clock_1_out), .D(or_12_out), .Q(out_12));  // open: Qn, preset, en, reset
  D_Flip_Flop d_ff_6 (.clk(clock_1_out), .D(or_13_out), .Q(out_15));  // open: Qn, preset, en, reset
  D_Flip_Flop d_ff_7 (.clk(clock_1_out), .D(or_14_out), .Q(out_17));  // open: Qn, preset, en, reset
  D_Flip_Flop d_ff_8 (.clk(clock_1_out), .D(or_15_out), .Q(out_19));  // open: Qn, preset, en, reset
  not not_4 (not_4_out, or_16_out);
  or or_16 (or_16_out, out_12, out_17, out_19, out_15);

  // Notes on the sheet:
  //   START
endmodule
