// Logisim project proyecto_logico.circ as structural Verilog
module P (
  input  NI,
  input  START,
  input  STOP,
  input  L0,
  input  L1,
  input  L2,
  input  L3,
  input  TZ,
  output DA,
  output DB,
  output DC,
  output V0,
  output V1,
  output V2,
  output V3,
  output MX,
  output TM,
  output PST
);

  wire and_1_out, and_2_out, and_3_out, and_4_out, and_5_out, and_6_out, and_7_out, and_8_out, and_9_out,
       and_10_out, and_11_out, and_18_out, and_19_out, clock_1_out, d_ff_1_q, d_ff_2_q, d_ff_3_q, not_1_out,
       not_2_out, not_3_out, not_4_out, not_5_out, not_6_out, not_7_out, not_8_out, not_9_out, not_10_out,
       not_11_out, not_12_out, not_13_out, not_14_out, not_15_out, not_16_out, not_17_out, not_18_out,
       not_19_out, not_20_out, not_21_out, not_22_out, not_23_out, not_24_out, not_25_out, not_26_out,
       not_27_out, not_28_out, not_29_out, not_30_out, not_31_out, not_32_out, not_33_out, not_34_out,
       not_35_out, not_36_out, not_37_out, not_38_out, not_39_out, not_40_out, not_41_out, or_1_out,
       or_2_out, or_3_out, or_4_out;

  not not_1 (not_1_out, d_ff_1_q);
  not not_2 (not_2_out, NI);
  not not_3 (not_3_out, d_ff_1_q);
  not not_4 (not_4_out, d_ff_3_q);
  not not_5 (not_5_out, d_ff_3_q);
  not not_6 (not_6_out, d_ff_2_q);
  not not_7 (not_7_out, d_ff_3_q);
  not not_8 (not_8_out, L0);
  not not_9 (not_9_out, d_ff_1_q);
  not not_10 (not_10_out, d_ff_2_q);
  not not_11 (not_11_out, d_ff_1_q);
  not not_12 (not_12_out, d_ff_1_q);
  not not_13 (not_13_out, d_ff_3_q);
  not not_14 (not_14_out, d_ff_3_q);
  not not_15 (not_15_out, TZ);
  not not_16 (not_16_out, d_ff_1_q);
  not not_17 (not_17_out, d_ff_2_q);
  not not_18 (not_18_out, d_ff_3_q);
  not not_19 (not_19_out, d_ff_1_q);
  not not_20 (not_20_out, d_ff_2_q);
  not not_21 (not_21_out, d_ff_1_q);
  not not_22 (not_22_out, L2);
  not not_23 (not_23_out, d_ff_2_q);
  not not_24 (not_24_out, d_ff_3_q);
  not not_25 (not_25_out, d_ff_1_q);
  not not_26 (not_26_out, d_ff_2_q);
  not not_27 (not_27_out, d_ff_1_q);
  not not_28 (not_28_out, d_ff_1_q);
  not not_29 (not_29_out, d_ff_3_q);
  not not_30 (not_30_out, d_ff_3_q);
  not not_31 (not_31_out, d_ff_3_q);
  not not_32 (not_32_out, TZ);
  not not_33 (not_33_out, STOP);
  not not_34 (not_34_out, d_ff_1_q);
  not not_35 (not_35_out, NI);
  not not_36 (not_36_out, d_ff_1_q);
  not not_37 (not_37_out, d_ff_3_q);
  and and_1 (and_1_out, not_1_out, d_ff_2_q, d_ff_3_q, L2, not_2_out);
  and and_2 (and_2_out, not_3_out, d_ff_2_q, not_4_out, L3);
  and and_3 (and_3_out, d_ff_1_q, d_ff_2_q, not_5_out);
  and and_4 (and_4_out, d_ff_1_q, not_6_out, not_7_out, not_8_out);
  and and_5 (and_5_out, not_9_out, not_10_out, d_ff_3_q, L1);
  and and_6 (and_6_out, not_11_out, d_ff_2_q, d_ff_3_q);
  and and_7 (and_7_out, not_12_out, d_ff_2_q, not_13_out);
  and and_8 (and_8_out, d_ff_1_q, d_ff_2_q, not_14_out, not_15_out);
  and and_9 (and_9_out, not_16_out, not_17_out, not_18_out, START);
  and and_10 (and_10_out, not_19_out, not_20_out, d_ff_3_q);
  and and_11 (and_11_out, not_21_out, d_ff_2_q, d_ff_3_q, not_22_out);
  and and_12 (V0, d_ff_1_q, not_23_out, not_24_out);
  and and_13 (V1, not_25_out, not_26_out, d_ff_3_q);
  and and_14 (V2, not_27_out, d_ff_2_q, d_ff_3_q);
  and and_15 (V3, not_28_out, d_ff_2_q, not_29_out);
  and and_16 (MX, d_ff_1_q, d_ff_2_q, not_30_out);
  and and_17 (TM, d_ff_1_q, d_ff_2_q, not_31_out, not_32_out, not_33_out);
  and and_18 (and_18_out, not_34_out, d_ff_2_q, d_ff_3_q, L2, not_35_out);
  and and_19 (and_19_out, not_36_out, d_ff_2_q, not_37_out, L3);
  not not_38 (not_38_out, STOP);
  or or_1 (or_1_out, and_1_out, and_2_out, and_3_out, and_4_out);
  not not_39 (not_39_out, STOP);
  or or_2 (or_2_out, and_5_out, and_6_out, and_7_out, and_8_out);
  not not_40 (not_40_out, STOP);
  or or_3 (or_3_out, and_9_out, and_10_out, and_11_out);
  not not_41 (not_41_out, STOP);
  or or_4 (or_4_out, and_18_out, and_19_out);
  and and_20 (DA, not_38_out, or_1_out);
  and and_21 (DB, not_39_out, or_2_out);
  and and_22 (DC, not_40_out, or_3_out);
  and and_23 (PST, not_41_out, or_4_out);
  Clock clock_1 (.out(clock_1_out));
  D_Flip_Flop d_ff_1 (.clk(clock_1_out), .D(DA), .Q(d_ff_1_q));  // open: Qn, preset, en, reset
  D_Flip_Flop d_ff_2 (.clk(clock_1_out), .D(DB), .Q(d_ff_2_q));  // open: Qn, preset, en, reset
  D_Flip_Flop d_ff_3 (.clk(clock_1_out), .D(DC), .Q(d_ff_3_q));  // open: Qn, preset, en, reset
endmodule
